# Fritzing sketch HC-06_phone (saved by Fritzing 0.9.2b)
breadboards: 1

parts:
  Part1 = Bluetooth HC-06 Macho
  Part2 = Arduino Uno (Rev3)
  R1 = Resistor [tolerance=±5% resistance=10k package=THT]
  R2 = Resistor [tolerance=±5% resistance=10k package=THT]
  R3 = Resistor [tolerance=±5% resistance=10k package=THT]

nets:
  N1: Part1.TXD, Part2.D0/RX
  N2: Part1.RXD, R1.Pin_0, R2.Pin_1
  VCC: Part1.VCC, Part2.5V
  GND: Part1.GND, Part2.GND
  N3: R1.Pin_1, R3.Pin_0
